# Fritzing sketch Circuit1B (saved by Fritzing 0.9.3b)
circuit board: 8.46667cm x 5.64444cm
breadboards: 1

parts:
  Part1 = Arduino Uno (Rev3)
  U1 = POT [package=3362u]
  R1 = Resistor [tolerance=±5% resistance=220 package=THT]
  LED1 = LED - 5mm [color="Red (633nm)" package="5 mm [THT]"]

nets:
  N1: Part1.A0, U1.S
  N2: Part1.D13/SCK, R1.Pin_1
  N3: Part1.5V, U1.A
  N4: Part1.GND, U1.E, LED1.anode
  N5: R1.Pin_0, LED1.cathode
