# Fritzing sketch Circuit1C (saved by Fritzing 0.9.3b)
circuit board: 8.46667cm x 5.64444cm
breadboards: 1

parts:
  R2 = Resistor [tolerance=±5% resistance=220 package=THT]
  LED1 = LED - 5mm [color="Red (633nm)" package="5 mm [THT]"]
  Part1 = Arduino Uno (Rev3)
  R1 = Resistor [tolerance=±5% resistance=220 package=THT]
  R3 = PHOTOCELL [package=photocell-kit]

nets:
  N1: R2.Pin_0, Part1.A0, R3.P$1
  N2: R2.Pin_1, LED1.cathode, LED1.anode, Part1.GND, R1.Pin_0
  N3: Part1.D13/SCK, R1.Pin_1
  N4: Part1.5V, R3.P$2
