# Fritzing sketch 4B (saved by Fritzing 0.9.3b)
circuit board: 8.46667cm x 5.64444cm
breadboards: 1

parts:
  Part1 = Arduino Uno (Rev3)
  U1 = LCD-16X2 [package=lcd-16x2_noholes]
  R1 = TRIMPOT [package=trimpot_pth_s3_lock]
  U2 = TMP36 [package=to-92-kit]

nets:
  N1: Part1.A0, U2.VOUT
  N2: Part1.D8, U1.DB7
  N3: Part1.D9_PWM, U1.DB6
  N4: Part1.D10_PWM/SS, U1.DB5
  N5: Part1.D11_PWM/MOSI, U1.DB4
  N6: Part1.D12/MISO, U1.E
  N7: Part1.D13/SCK, U1.RS
  GND: Part1.GND, U1.VSS, U1.R_W, U1.K, R1.CW, U2.GND
  5V: Part1.5V, U1.VDD, U1.A, R1.CCW, U2.VCC
  N8: U1.VO, R1.WIPER

// code stored in the sketch: 4c.ino
/*
SparkFun Inventor?s Kit
Circuit 4B - Temperature Sensor

The LCD will display readings from a temperature sensor in degrees Celsius and Fahrenheit.

This sketch was written by SparkFun Electronics, with lots of help from the Arduino community.
This code is completely free for any use.

View circuit diagram and instructions at: https://learn.sparkfun.com/tutorials/sparkfun-inventors-kit-experiment-guide---v40
Download drawings and code at: https://github.com/sparkfun/SIK-Guide-Code
*/

#include <LiquidCrystal.h>                  //the liquid crystal libarry contains commands for printing to the display
LiquidCrystal lcd(13, 12, 11, 10, 9, 8);    // tell the RedBoard what pins are connected to the display

float voltage = 0;                          //the voltage measured from the TMP36
float degreesC = 0;                         //the temperature in Celsius, calcuated from the voltage
float degreesF = 0;                         //the temperature in Farenheit, calcuated from the voltage

void setup() {

  lcd.begin(16, 2);                         //tell the lcd library that we are using a display that is 16 characters wide and 2 characters high
  lcd.clear();                              //clear the display    
}

void loop() {
  
  voltage = analogRead(A0) * 0.004882814;   //convert the analog reading, which varies from 0 to 1023, back to a voltage value from 0-5 volts
  degreesC = (voltage - 0.5) * 100.0;       //convert the voltage to a temperature in degrees Celsius
  degreesF = degreesC * (9.0/5.0) + 32.0;   //convert the voltage to a temperature in dgrees Fahrenheit

  lcd.clear();                              //clear the LCD

  lcd.setCursor(0,0);                       //set the cursor to the top left position
  lcd.print("Degrees C: ");                 //print a label for the data
  lcd.print(degreesC);                      //print the degrees Celsius
  
  lcd.setCursor(0,1);                       //set the cursor to the lower left position
  lcd.print("Degrees F: ");                 //Print a label for the data
  lcd.print(degreesF);                      //print the degrees Fahreheit
  
  delay(1000);                              //delay for 1 second between each reading (this makes the display less noisy)
}
