# Fritzing sketch 5C (saved by Fritzing 0.9.3b)
circuit board: 8.46667cm x 5.64444cm
breadboards: 1

parts:
  Part1 = Arduino Uno (Rev3)
  Part2 = Motor Driver 1A Dual TB6612FNG
  S1 = Toggle Switch [package=THT]
  M1 = DC Motor
  M2 = DC Motor
  hc-sr1 = hc-sr04

nets (from the schematic view):
  N1: Part1.D8, Part2.BIN1
  N2: Part1.D9_PWM, Part2.BIN2
  N3: Part1.D10_PWM/SS, Part2.PWMB
  N4: Part1.D11_PWM/MOSI, Part2.PWMA
  N5: Part1.D12/MISO, Part2.AIN2
  GND: Part1.GND, hc-sr1.GND
  N6: Part1.D5_PWM, hc-sr1.Trig
  N7: Part1.D6_PWM, hc-sr1.Echo
  N8: Part1.D7, S1.L1
  VCC: Part1.5V, Part1.VIN, Part2.VCC, Part2.VM, Part2.STBY, hc-sr1.VCC
  N9: Part2.B01, Part2.B02, M2.pin_1, M2.pin_2
  N10: Part2.A02, M1.pin_2
  N11: Part2.A01, M1.pin_1
