# Fritzing sketch Final - Project (saved by Fritzing 0.9.3b)
circuit board: 5.64444cm x 8.46667cm
circuit board: 5.64444cm x 8.46667cm
circuit board: 5.64444cm x 8.46667cm
breadboards: 1

parts:
  Part1 = Arduino Uno (Rev3)
  J1 = Basic Servo
  J2 = Basic Servo
  J3 = Basic Servo
  J4 = Basic Servo
  J5 = Basic Servo
  J6 = Basic Servo
  J7 = Basic Servo
  S1 = Pushbutton [package="[THT]"]
  S2 = Pushbutton [package="[THT]"]
  S3 = Pushbutton [package="[THT]"]
  S4 = Pushbutton [package="[THT]"]
  S5 = Pushbutton [package="[THT]"]
  LED1 = LED - 3mm [color="Red (633nm)" package="3 mm [THT]"]

nets:
  N1: Part1.D8, J1.pulse
  N2: Part1.D9_PWM, J2.pulse
  N3: Part1.D10_PWM/SS, J3.pulse
  N4: Part1.D11_PWM/MOSI, J4.pulse
  N5: Part1.D12/MISO, J5.pulse
  N6: Part1.D13/SCK, J6.pulse
  GND: Part1.GND, J1.gnd, J2.gnd, J3.gnd, J4.gnd, J5.gnd, J6.gnd, J7.gnd, S1.Pin_3, S1.Pin_4, S2.Pin_3, S2.Pin_4, S3.Pin_3, S3.Pin_4, S4.Pin_3, S4.Pin_4, S5.Pin_3, S5.Pin_4, LED1.cathode
  N7: Part1.D0/RX, LED1.anode
  N8: Part1.D2, S5.Pin_1, S5.Pin_2
  N9: Part1.D3_PWM, S1.Pin_1, S1.Pin_2
  N10: Part1.D4, S2.Pin_1, S2.Pin_2
  N11: Part1.D5_PWM, S3.Pin_1, S3.Pin_2
  N12: Part1.D6_PWM, S4.Pin_1, S4.Pin_2
  N13: Part1.D7, J7.pulse
  VCC: Part1.3V3, J1.vcc, J2.vcc, J3.vcc, J4.vcc, J5.vcc, J6.vcc, J7.vcc
